# Fritzing sketch overview (saved by Fritzing 0.9.3b)

parts:
  Raspberry_Pi1 = Raspberry Pi 2
  M1 = DC Motor
  M2 = DC Motor
  M3 = DC Motor
  M4 = DC Motor
  U1 = TCM8240MD [package=tcm8240md]  # not connected
  S1 = H-Bridge with L298N
  VCC1 = Battery block 9V

nets:
  N1: Raspberry_Pi1.GPIO17, S1.IN1
  N2: Raspberry_Pi1.GPIO22, S1.IN2
  N3: Raspberry_Pi1.3V3, S1.IN3
  N4: Raspberry_Pi1.GPIO24, S1.IN4
  GND: Raspberry_Pi1.GND, S1.GND, VCC1.-
  N5: M1.pin_1, M2.pin_1, S1.M1-02
  N6: M1.pin_2, M2.pin_2, S1.M1-01
  N7: M3.pin_1, M4.pin_1, S1.M2-02
  N8: M3.pin_2, M4.pin_2, S1.M2-01
  N9: S1.12V, VCC1.+

custom parts:
  H-Bridge with L298N: h-bridge
